# Fritzing sketch strix-takeover-breadboard (saved by Fritzing 1.0.3)
breadboards: 1

parts:
  Nano1 = Arduino Nano (Rev3.0)
  R1 = Resistor [resistance=4.7kΩ package=THT]
  C1 = Ceramic Capacitor [capacitance=1µF package="100 mil [THT, multilayer]"]
  R2 = Resistor [resistance=4.7kΩ package=THT]
  C2 = Ceramic Capacitor [capacitance=1µF package="100 mil [THT, multilayer]"]
  SR04_frontLeft = HC-SR04 Ultrasonic Distance Sensor
  SR04_frontRight = HC-SR04 Ultrasonic Distance Sensor
  LevelShifter1 = I2C level shifter bidirectional
  ToF_VL53L4CD = Header 4 [package=jst-4-pth]

nets:
  GND: Nano1.GND, C1.1, C2.1, SR04_frontLeft.GND, SR04_frontRight.GND, LevelShifter1.GND, ToF_VL53L4CD.4
  N1: Nano1.D2, SR04_frontLeft.TRIG
  N2: Nano1.D3, SR04_frontLeft.ECHO
  N3: Nano1.D4, SR04_frontRight.TRIG
  N4: Nano1.D5, SR04_frontRight.ECHO
  N5: Nano1.D9, R1.Pin_0
  N6: Nano1.D10, R2.Pin_0
  VCC: Nano1.5V, SR04_frontLeft.VCC, SR04_frontRight.VCC, LevelShifter1.HV
  N7: Nano1.A5, LevelShifter1.HV2
  N8: Nano1.A4, LevelShifter1.HV1
  N9: Nano1.3V3, LevelShifter1.LV, ToF_VL53L4CD.3
  N10: R1.Pin_1, C1.0
  N11: R2.Pin_1, C2.0
  N12: LevelShifter1.LV2, ToF_VL53L4CD.2
  N13: LevelShifter1.LV1, ToF_VL53L4CD.1

notes:
  STRIX - controller takeover, Variant B (PWM wiper synthesis)
  The Nano synthesizes the two wiper voltages that the handheld
  controller's trigger and steering pots used to produce. Each
  channel is a 4.7k + 1uF RC low-pass filter on a Timer1 PWM pin.
  D9 = throttle, D10 = steering, A0 = controller rail sense.
  ORANGE (A0): to the controller's pot HIGH / rail pin.
  Scales every duty to the sagging AA rail so calibrated
  neutral cannot drift. Do not omit this wire.
  Nano is rotated so the USB end faces the board edge; the
  phone's OTG cable exits left and powers the Nano.
  BLUE -> controller TRIGGER pot WIPER pin
  GREEN -> controller WHEEL pot WIPER pin
  BLACK -> controller GROUND (pot LOW pin)
  Identify which harness wire is the wiper before cutting:
  see docs/pot-identification.md. On this build's Hosim
  controller the BLACK harness wire was the wiper.
  FORWARD-PERCEPTION ARRAY
  HC-SR04 ultrasonics, front-left and front-right corners:
  TRIG/ECHO -> D2/D3 (left), D4/D5 (right), 5V + GND rails.
  Mount them on the corners angled ~15 deg outward, at bumper
  height. Left/right is the CAR's perspective, not yours.
  See docs/sensor-wiring.md for placement and aiming.
  3.3V TIME-OF-FLIGHT SENSOR (centre beam)
  The 4-pin header stands in for the VL53L4CD / Modulino
  Distance module - Fritzing has no part for it.
  SDA/SCL cross a bidirectional I2C level shifter because the
  Nano's I2C is 5V logic and the module is 3.3V-only and NOT
  5V tolerant. HV side faces the Nano (A4/A5 + 5V), LV side
  faces the module.
  ORANGE 3V3 comes straight off the Nano's 3V3 pin, never a
  5V rail, and drives only this module (~50mA budget).
